# Fritzing sketch IRSensor fritzing (saved by Fritzing 0.9.3b)

parts:
  Arduino_UNO = Arduino Uno (Rev3) - ICSP
  IR_Sensor = fc-51 [package=THT]

nets:
  N1: Arduino_UNO.D2, IR_Sensor.pin1
  N2: Arduino_UNO.5V, IR_Sensor.pin3
  N3: Arduino_UNO.GND, IR_Sensor.pin2
