# Fritzing sketch Ultrasonic Sensor Fritzing (saved by Fritzing 0.9.3b)

parts:
  Arduino_UNO = Arduino Uno (Rev3) - ICSP
  HC-SR04_Sensor_1 = HC-SR04 Ultrasonic Distance Sensor

nets:
  N1: Arduino_UNO.D9_PWM, HC-SR04_Sensor_1.TRIG
  N2: Arduino_UNO.D10_PWM/SS, HC-SR04_Sensor_1.ECHO
  5V: Arduino_UNO.5V, HC-SR04_Sensor_1.VCC
  GND: Arduino_UNO.GND, HC-SR04_Sensor_1.GND
